// Digital circuit alu_ac.dig as structural Verilog
module alu_ac (
  input  [7:0] A,
  input  [3:0] Op,
  output [3:0] S2,
  output [3:0] S1
);

  wire eq_out, soma_8bit_1_co, subtracao_8bit_1_co;
  wire [7:0] divisor_ac, divisor_mq, multiplexer_1_out, multiplicador_ac, multiplicador_mq, \nand ,
       shift_left, shift_right, soma, subtracao, \xor ;

  soma_8bit soma_8bit_1 (.A({S1, S2}), .B(A), .S1(soma[3:0]), .Co(soma_8bit_1_co), .S2(soma[7:4]));
  subtracao_8bit subtracao_8bit_1 (
    .A({S1, S2}), .B(A), .Sel(1'b1), .S1(subtracao[3:0]), .Co(subtracao_8bit_1_co), .S2(subtracao[7:4]));
  multiplicacao_8bit multiplicacao_8bit_1 (.A({S1, S2}), .B(A), .AC(multiplicador_ac), .MQ(multiplicador_mq));
  divisor_8bit divisor_8bit_1 (.A({S1, S2}), .B(A), .MQ(divisor_mq), .AC(divisor_ac));
  shift_left shift_left_1 (.A(A), .S(shift_left));
  shift_right shift_right_1 (.A(A), .S(shift_right));
  \nand  nand_1 (.A({S1, S2}), .B(A), .S(\nand ));
  \xor  xor_1 (.A({S1, S2}), .B(A), .S(\xor ));
  LED led_1 (.in(subtracao_8bit_1_co));
  LED led_2 (.in(soma_8bit_1_co));
  Multiplexer #(.Selector_Bits(4), .Bits(8)) multiplexer_1 (
    .sel(Op), .in_0(soma), .in_1(subtracao), .in_2(multiplicador_ac), .in_3(multiplicador_mq),
    .in_4(divisor_mq), .in_5(divisor_ac), .in_6(shift_left), .in_7(shift_right), .in_8(\nand ), .in_9(\xor ),
    .in_10({8{1'b0}}), .in_11({8{1'b0}}), .in_12({8{1'b0}}), .in_13({8{1'b0}}), .in_14({8{1'b0}}),
    .in_15({8{1'b0}}), .out(multiplexer_1_out));
  Register #(.Bits(8)) register_1 (.D(multiplexer_1_out), .C(eq_out), .en(1'b1), .Q({S1, S2}));
  Button eq (.out(eq_out));

  // Other names for the same wires on the sheet: Q[7:0] = {S1, S2}
endmodule
