// Digital circuit divisor_8bit.dig as structural Verilog
module divisor_8bit (
  input  [7:0] A,
  input  [7:0] B,
  output [7:0] MQ,
  output [7:0] AC
);

  wire R0_0, R0_1, R0_2, R0_3, R0_4, R0_5, R0_6, R0_7, R1_0, R1_1, R1_2, R1_3, R1_4, R1_5, R1_6, R1_7, R2_0,
       R2_1, R2_2, R2_3, R2_4, R2_5, R2_6, R2_7, R3_0, R3_1, R3_2, R3_3, R3_4, R3_5, R3_6, R3_7, R4_0, R4_1,
       R4_2, R4_3, R4_4, R4_5, R4_6, R4_7, R5_0, R5_1, R5_2, R5_3, R5_4, R5_5, R5_6, R5_7, R6_0, R6_1, R6_2,
       R6_3, R6_4, R6_5, R6_6, R6_7, subtracao_restauracao_9_co, subtracao_restauracao_10_co,
       subtracao_restauracao_11_co, subtracao_restauracao_12_co, subtracao_restauracao_13_co,
       subtracao_restauracao_14_co, subtracao_restauracao_15_co, subtracao_restauracao_16_co,
       subtracao_restauracao_17_co, subtracao_restauracao_18_co, subtracao_restauracao_19_co,
       subtracao_restauracao_20_co, subtracao_restauracao_21_co, subtracao_restauracao_22_co,
       subtracao_restauracao_23_co, subtracao_restauracao_24_co, subtracao_restauracao_25_co,
       subtracao_restauracao_26_co, subtracao_restauracao_27_co, subtracao_restauracao_28_co,
       subtracao_restauracao_29_co, subtracao_restauracao_30_co, subtracao_restauracao_31_co,
       subtracao_restauracao_32_co, subtracao_restauracao_33_co, subtracao_restauracao_34_co,
       subtracao_restauracao_35_co, subtracao_restauracao_36_co, subtracao_restauracao_37_co,
       subtracao_restauracao_38_co, subtracao_restauracao_39_co, subtracao_restauracao_40_co,
       subtracao_restauracao_41_co, subtracao_restauracao_42_co, subtracao_restauracao_43_co,
       subtracao_restauracao_44_co, subtracao_restauracao_45_co, subtracao_restauracao_46_co,
       subtracao_restauracao_47_co, subtracao_restauracao_48_co, subtracao_restauracao_49_co,
       subtracao_restauracao_50_co, subtracao_restauracao_51_co, subtracao_restauracao_52_co,
       subtracao_restauracao_53_co, subtracao_restauracao_54_co, subtracao_restauracao_55_co,
       subtracao_restauracao_56_co, subtracao_restauracao_57_co, subtracao_restauracao_58_co,
       subtracao_restauracao_59_co, subtracao_restauracao_60_co, subtracao_restauracao_61_co,
       subtracao_restauracao_62_co, subtracao_restauracao_63_co, subtracao_restauracao_64_co;

  subtracao_restauracao subtracao_restauracao_1 (
    .A(1'b0), .B(B[7]), .Ci(subtracao_restauracao_9_co), .Sel(MQ[7]), .Co(MQ[7]), .R(R0_0));
  subtracao_restauracao subtracao_restauracao_2 (
    .A(R0_1), .B(B[7]), .Ci(subtracao_restauracao_10_co), .Sel(MQ[6]), .Co(MQ[6]), .R(R1_0));
  subtracao_restauracao subtracao_restauracao_3 (
    .A(R1_1), .B(B[7]), .Ci(subtracao_restauracao_11_co), .Sel(MQ[5]), .Co(MQ[5]), .R(R2_0));
  subtracao_restauracao subtracao_restauracao_4 (
    .A(R2_1), .B(B[7]), .Ci(subtracao_restauracao_12_co), .Sel(MQ[4]), .Co(MQ[4]), .R(R3_0));
  subtracao_restauracao subtracao_restauracao_5 (
    .A(R3_1), .B(B[7]), .Ci(subtracao_restauracao_13_co), .Sel(MQ[3]), .Co(MQ[3]), .R(R4_0));
  subtracao_restauracao subtracao_restauracao_6 (
    .A(R4_1), .B(B[7]), .Ci(subtracao_restauracao_14_co), .Sel(MQ[2]), .Co(MQ[2]), .R(R5_0));
  subtracao_restauracao subtracao_restauracao_7 (
    .A(R5_1), .B(B[7]), .Ci(subtracao_restauracao_15_co), .Sel(MQ[1]), .Co(MQ[1]), .R(R6_0));
  subtracao_restauracao subtracao_restauracao_8 (
    .A(R6_1), .B(B[7]), .Ci(subtracao_restauracao_16_co), .Sel(MQ[0]), .Co(MQ[0]), .R(AC[7]));
  subtracao_restauracao subtracao_restauracao_9 (
    .A(1'b0), .B(B[6]), .Ci(subtracao_restauracao_17_co), .Sel(MQ[7]), .Co(subtracao_restauracao_9_co),
    .R(R0_1));
  subtracao_restauracao subtracao_restauracao_10 (
    .A(R0_2), .B(B[6]), .Ci(subtracao_restauracao_18_co), .Sel(MQ[6]), .Co(subtracao_restauracao_10_co),
    .R(R1_1));
  subtracao_restauracao subtracao_restauracao_11 (
    .A(R1_2), .B(B[6]), .Ci(subtracao_restauracao_19_co), .Sel(MQ[5]), .Co(subtracao_restauracao_11_co),
    .R(R2_1));
  subtracao_restauracao subtracao_restauracao_12 (
    .A(R2_2), .B(B[6]), .Ci(subtracao_restauracao_20_co), .Sel(MQ[4]), .Co(subtracao_restauracao_12_co),
    .R(R3_1));
  subtracao_restauracao subtracao_restauracao_13 (
    .A(R3_2), .B(B[6]), .Ci(subtracao_restauracao_21_co), .Sel(MQ[3]), .Co(subtracao_restauracao_13_co),
    .R(R4_1));
  subtracao_restauracao subtracao_restauracao_14 (
    .A(R4_2), .B(B[6]), .Ci(subtracao_restauracao_22_co), .Sel(MQ[2]), .Co(subtracao_restauracao_14_co),
    .R(R5_1));
  subtracao_restauracao subtracao_restauracao_15 (
    .A(R5_2), .B(B[6]), .Ci(subtracao_restauracao_23_co), .Sel(MQ[1]), .Co(subtracao_restauracao_15_co),
    .R(R6_1));
  subtracao_restauracao subtracao_restauracao_16 (
    .A(R6_2), .B(B[6]), .Ci(subtracao_restauracao_24_co), .Sel(MQ[0]), .Co(subtracao_restauracao_16_co),
    .R(AC[6]));
  subtracao_restauracao subtracao_restauracao_17 (
    .A(1'b0), .B(B[5]), .Ci(subtracao_restauracao_25_co), .Sel(MQ[7]), .Co(subtracao_restauracao_17_co),
    .R(R0_2));
  subtracao_restauracao subtracao_restauracao_18 (
    .A(R0_3), .B(B[5]), .Ci(subtracao_restauracao_26_co), .Sel(MQ[6]), .Co(subtracao_restauracao_18_co),
    .R(R1_2));
  subtracao_restauracao subtracao_restauracao_19 (
    .A(R1_3), .B(B[5]), .Ci(subtracao_restauracao_27_co), .Sel(MQ[5]), .Co(subtracao_restauracao_19_co),
    .R(R2_2));
  subtracao_restauracao subtracao_restauracao_20 (
    .A(R2_3), .B(B[5]), .Ci(subtracao_restauracao_28_co), .Sel(MQ[4]), .Co(subtracao_restauracao_20_co),
    .R(R3_2));
  subtracao_restauracao subtracao_restauracao_21 (
    .A(R3_3), .B(B[5]), .Ci(subtracao_restauracao_29_co), .Sel(MQ[3]), .Co(subtracao_restauracao_21_co),
    .R(R4_2));
  subtracao_restauracao subtracao_restauracao_22 (
    .A(R4_3), .B(B[5]), .Ci(subtracao_restauracao_30_co), .Sel(MQ[2]), .Co(subtracao_restauracao_22_co),
    .R(R5_2));
  subtracao_restauracao subtracao_restauracao_23 (
    .A(R5_3), .B(B[5]), .Ci(subtracao_restauracao_31_co), .Sel(MQ[1]), .Co(subtracao_restauracao_23_co),
    .R(R6_2));
  subtracao_restauracao subtracao_restauracao_24 (
    .A(R6_3), .B(B[5]), .Ci(subtracao_restauracao_32_co), .Sel(MQ[0]), .Co(subtracao_restauracao_24_co),
    .R(AC[5]));
  subtracao_restauracao subtracao_restauracao_25 (
    .A(1'b0), .B(B[4]), .Ci(subtracao_restauracao_33_co), .Sel(MQ[7]), .Co(subtracao_restauracao_25_co),
    .R(R0_3));
  subtracao_restauracao subtracao_restauracao_26 (
    .A(R0_4), .B(B[4]), .Ci(subtracao_restauracao_34_co), .Sel(MQ[6]), .Co(subtracao_restauracao_26_co),
    .R(R1_3));
  subtracao_restauracao subtracao_restauracao_27 (
    .A(R1_4), .B(B[4]), .Ci(subtracao_restauracao_35_co), .Sel(MQ[5]), .Co(subtracao_restauracao_27_co),
    .R(R2_3));
  subtracao_restauracao subtracao_restauracao_28 (
    .A(R2_4), .B(B[4]), .Ci(subtracao_restauracao_36_co), .Sel(MQ[4]), .Co(subtracao_restauracao_28_co),
    .R(R3_3));
  subtracao_restauracao subtracao_restauracao_29 (
    .A(R3_4), .B(B[4]), .Ci(subtracao_restauracao_37_co), .Sel(MQ[3]), .Co(subtracao_restauracao_29_co),
    .R(R4_3));
  subtracao_restauracao subtracao_restauracao_30 (
    .A(R4_4), .B(B[4]), .Ci(subtracao_restauracao_38_co), .Sel(MQ[2]), .Co(subtracao_restauracao_30_co),
    .R(R5_3));
  subtracao_restauracao subtracao_restauracao_31 (
    .A(R5_4), .B(B[4]), .Ci(subtracao_restauracao_39_co), .Sel(MQ[1]), .Co(subtracao_restauracao_31_co),
    .R(R6_3));
  subtracao_restauracao subtracao_restauracao_32 (
    .A(R6_4), .B(B[4]), .Ci(subtracao_restauracao_40_co), .Sel(MQ[0]), .Co(subtracao_restauracao_32_co),
    .R(AC[4]));
  subtracao_restauracao subtracao_restauracao_33 (
    .A(1'b0), .B(B[3]), .Ci(subtracao_restauracao_41_co), .Sel(MQ[7]), .Co(subtracao_restauracao_33_co),
    .R(R0_4));
  subtracao_restauracao subtracao_restauracao_34 (
    .A(R0_5), .B(B[3]), .Ci(subtracao_restauracao_42_co), .Sel(MQ[6]), .Co(subtracao_restauracao_34_co),
    .R(R1_4));
  subtracao_restauracao subtracao_restauracao_35 (
    .A(R1_5), .B(B[3]), .Ci(subtracao_restauracao_43_co), .Sel(MQ[5]), .Co(subtracao_restauracao_35_co),
    .R(R2_4));
  subtracao_restauracao subtracao_restauracao_36 (
    .A(R2_5), .B(B[3]), .Ci(subtracao_restauracao_44_co), .Sel(MQ[4]), .Co(subtracao_restauracao_36_co),
    .R(R3_4));
  subtracao_restauracao subtracao_restauracao_37 (
    .A(R3_5), .B(B[3]), .Ci(subtracao_restauracao_45_co), .Sel(MQ[3]), .Co(subtracao_restauracao_37_co),
    .R(R4_4));
  subtracao_restauracao subtracao_restauracao_38 (
    .A(R4_5), .B(B[3]), .Ci(subtracao_restauracao_46_co), .Sel(MQ[2]), .Co(subtracao_restauracao_38_co),
    .R(R5_4));
  subtracao_restauracao subtracao_restauracao_39 (
    .A(R5_5), .B(B[3]), .Ci(subtracao_restauracao_47_co), .Sel(MQ[1]), .Co(subtracao_restauracao_39_co),
    .R(R6_4));
  subtracao_restauracao subtracao_restauracao_40 (
    .A(R6_5), .B(B[3]), .Ci(subtracao_restauracao_48_co), .Sel(MQ[0]), .Co(subtracao_restauracao_40_co),
    .R(AC[3]));
  subtracao_restauracao subtracao_restauracao_41 (
    .A(1'b0), .B(B[2]), .Ci(subtracao_restauracao_49_co), .Sel(MQ[7]), .Co(subtracao_restauracao_41_co),
    .R(R0_5));
  subtracao_restauracao subtracao_restauracao_42 (
    .A(R0_6), .B(B[2]), .Ci(subtracao_restauracao_50_co), .Sel(MQ[6]), .Co(subtracao_restauracao_42_co),
    .R(R1_5));
  subtracao_restauracao subtracao_restauracao_43 (
    .A(R1_6), .B(B[2]), .Ci(subtracao_restauracao_51_co), .Sel(MQ[5]), .Co(subtracao_restauracao_43_co),
    .R(R2_5));
  subtracao_restauracao subtracao_restauracao_44 (
    .A(R2_6), .B(B[2]), .Ci(subtracao_restauracao_52_co), .Sel(MQ[4]), .Co(subtracao_restauracao_44_co),
    .R(R3_5));
  subtracao_restauracao subtracao_restauracao_45 (
    .A(R3_6), .B(B[2]), .Ci(subtracao_restauracao_53_co), .Sel(MQ[3]), .Co(subtracao_restauracao_45_co),
    .R(R4_5));
  subtracao_restauracao subtracao_restauracao_46 (
    .A(R4_6), .B(B[2]), .Ci(subtracao_restauracao_54_co), .Sel(MQ[2]), .Co(subtracao_restauracao_46_co),
    .R(R5_5));
  subtracao_restauracao subtracao_restauracao_47 (
    .A(R5_6), .B(B[2]), .Ci(subtracao_restauracao_55_co), .Sel(MQ[1]), .Co(subtracao_restauracao_47_co),
    .R(R6_5));
  subtracao_restauracao subtracao_restauracao_48 (
    .A(R6_6), .B(B[2]), .Ci(subtracao_restauracao_56_co), .Sel(MQ[0]), .Co(subtracao_restauracao_48_co),
    .R(AC[2]));
  subtracao_restauracao subtracao_restauracao_49 (
    .A(1'b0), .B(B[1]), .Ci(subtracao_restauracao_57_co), .Sel(MQ[7]), .Co(subtracao_restauracao_49_co),
    .R(R0_6));
  subtracao_restauracao subtracao_restauracao_50 (
    .A(R0_7), .B(B[1]), .Ci(subtracao_restauracao_58_co), .Sel(MQ[6]), .Co(subtracao_restauracao_50_co),
    .R(R1_6));
  subtracao_restauracao subtracao_restauracao_51 (
    .A(R1_7), .B(B[1]), .Ci(subtracao_restauracao_59_co), .Sel(MQ[5]), .Co(subtracao_restauracao_51_co),
    .R(R2_6));
  subtracao_restauracao subtracao_restauracao_52 (
    .A(R2_7), .B(B[1]), .Ci(subtracao_restauracao_60_co), .Sel(MQ[4]), .Co(subtracao_restauracao_52_co),
    .R(R3_6));
  subtracao_restauracao subtracao_restauracao_53 (
    .A(R3_7), .B(B[1]), .Ci(subtracao_restauracao_61_co), .Sel(MQ[3]), .Co(subtracao_restauracao_53_co),
    .R(R4_6));
  subtracao_restauracao subtracao_restauracao_54 (
    .A(R4_7), .B(B[1]), .Ci(subtracao_restauracao_62_co), .Sel(MQ[2]), .Co(subtracao_restauracao_54_co),
    .R(R5_6));
  subtracao_restauracao subtracao_restauracao_55 (
    .A(R5_7), .B(B[1]), .Ci(subtracao_restauracao_63_co), .Sel(MQ[1]), .Co(subtracao_restauracao_55_co),
    .R(R6_6));
  subtracao_restauracao subtracao_restauracao_56 (
    .A(R6_7), .B(B[1]), .Ci(subtracao_restauracao_64_co), .Sel(MQ[0]), .Co(subtracao_restauracao_56_co),
    .R(AC[1]));
  subtracao_restauracao subtracao_restauracao_57 (
    .A(A[7]), .B(B[0]), .Ci(1'b1), .Sel(MQ[7]), .Co(subtracao_restauracao_57_co), .R(R0_7));
  subtracao_restauracao subtracao_restauracao_58 (
    .A(A[6]), .B(B[0]), .Ci(1'b1), .Sel(MQ[6]), .Co(subtracao_restauracao_58_co), .R(R1_7));
  subtracao_restauracao subtracao_restauracao_59 (
    .A(A[5]), .B(B[0]), .Ci(1'b1), .Sel(MQ[5]), .Co(subtracao_restauracao_59_co), .R(R2_7));
  subtracao_restauracao subtracao_restauracao_60 (
    .A(A[4]), .B(B[0]), .Ci(1'b1), .Sel(MQ[4]), .Co(subtracao_restauracao_60_co), .R(R3_7));
  subtracao_restauracao subtracao_restauracao_61 (
    .A(A[3]), .B(B[0]), .Ci(1'b1), .Sel(MQ[3]), .Co(subtracao_restauracao_61_co), .R(R4_7));
  subtracao_restauracao subtracao_restauracao_62 (
    .A(A[2]), .B(B[0]), .Ci(1'b1), .Sel(MQ[2]), .Co(subtracao_restauracao_62_co), .R(R5_7));
  subtracao_restauracao subtracao_restauracao_63 (
    .A(A[1]), .B(B[0]), .Ci(1'b1), .Sel(MQ[1]), .Co(subtracao_restauracao_63_co), .R(R6_7));
  subtracao_restauracao subtracao_restauracao_64 (
    .A(A[0]), .B(B[0]), .Ci(1'b1), .Sel(MQ[0]), .Co(subtracao_restauracao_64_co), .R(AC[0]));

  // Other names for the same wires on the sheet: R7_0 = AC[7]; R7_1 = AC[6]; R7_2 = AC[5]; R7_3 = AC[4]; R7_4 = AC[3];
  //   R7_5 = AC[2]; R7_6 = AC[1]; R7_7 = AC[0]
endmodule
