// Digital circuit multiplicacao_8bit.dig as structural Verilog
module multiplicacao_8bit (
  input  [7:0] A,
  input  [7:0] B,
  output [7:0] AC,
  output [7:0] MQ
);

  wire and_1_out, and_2_out, and_3_out, and_4_out, and_5_out, and_6_out, and_7_out, and_8_out, and_9_out,
       and_10_out, and_11_out, and_12_out, and_13_out, and_14_out, and_15_out, and_16_out, and_17_out,
       and_18_out, and_19_out, and_20_out, and_21_out, and_22_out, and_23_out, and_24_out, and_25_out,
       and_26_out, and_27_out, and_28_out, and_29_out, and_30_out, and_31_out, and_32_out, and_33_out,
       and_34_out, and_35_out, and_36_out, and_37_out, and_38_out, and_39_out, and_40_out, and_41_out,
       and_42_out, and_43_out, and_44_out, and_45_out, and_46_out, and_47_out, and_48_out, and_49_out,
       and_50_out, and_51_out, and_52_out, and_53_out, and_54_out, and_55_out, and_56_out, and_57_out,
       and_58_out, and_59_out, and_60_out, and_61_out, and_62_out, and_63_out, and_64_out, Co_0, Co_1, Co_2,
       Co_3, Co_4, Co_5, Co_6, S0_1, S0_2, S0_3, S0_4, S0_5, S0_6, S0_7, S1_1, S1_2, S1_3, S1_4, S1_5, S1_6,
       S1_7, S2_1, S2_2, S2_3, S2_4, S2_5, S2_6, S2_7, S3_1, S3_2, S3_3, S3_4, S3_5, S3_6, S3_7, S4_1, S4_2,
       S4_3, S4_4, S4_5, S4_6, S4_7, S5_1, S5_2, S5_3, S5_4, S5_5, S5_6, S5_7, S6_1, S6_2, S6_3, S6_4, S6_5,
       S6_6, S6_7, soma_1bit_1_co, soma_1bit_2_co, soma_1bit_3_co, soma_1bit_4_co, soma_1bit_5_co,
       soma_1bit_6_co, soma_1bit_7_co, soma_1bit_8_co, soma_1bit_9_co, soma_1bit_10_co, soma_1bit_11_co,
       soma_1bit_12_co, soma_1bit_13_co, soma_1bit_14_co, soma_1bit_15_co, soma_1bit_16_co, soma_1bit_17_co,
       soma_1bit_18_co, soma_1bit_19_co, soma_1bit_20_co, soma_1bit_21_co, soma_1bit_22_co, soma_1bit_23_co,
       soma_1bit_24_co, soma_1bit_25_co, soma_1bit_26_co, soma_1bit_27_co, soma_1bit_28_co, soma_1bit_29_co,
       soma_1bit_30_co, soma_1bit_31_co, soma_1bit_32_co, soma_1bit_33_co, soma_1bit_34_co, soma_1bit_35_co,
       soma_1bit_36_co, soma_1bit_37_co, soma_1bit_38_co, soma_1bit_39_co, soma_1bit_40_co, soma_1bit_41_co,
       soma_1bit_42_co, soma_1bit_43_co, soma_1bit_44_co, soma_1bit_45_co, soma_1bit_46_co, soma_1bit_47_co,
       soma_1bit_48_co, soma_1bit_49_co, soma_1bit_50_co, soma_1bit_51_co, soma_1bit_52_co, soma_1bit_53_co,
       soma_1bit_54_co, soma_1bit_55_co, soma_1bit_56_co;

  and and_1 (and_1_out, A[0], B[0]);
  and and_2 (and_2_out, A[0], B[1]);
  and and_3 (and_3_out, A[0], B[2]);
  and and_4 (and_4_out, A[0], B[3]);
  and and_5 (and_5_out, A[0], B[4]);
  and and_6 (and_6_out, A[0], B[5]);
  and and_7 (and_7_out, A[0], B[6]);
  and and_8 (and_8_out, A[0], B[7]);
  soma_1bit soma_1bit_1 (.A(1'b0), .B(and_1_out), .Ci(1'b0), .S(AC[0]), .Co(soma_1bit_1_co));
  soma_1bit soma_1bit_2 (.A(S0_1), .B(and_2_out), .Ci(1'b0), .S(AC[1]), .Co(soma_1bit_2_co));
  soma_1bit soma_1bit_3 (.A(S1_1), .B(and_3_out), .Ci(1'b0), .S(AC[2]), .Co(soma_1bit_3_co));
  soma_1bit soma_1bit_4 (.A(S2_1), .B(and_4_out), .Ci(1'b0), .S(AC[3]), .Co(soma_1bit_4_co));
  soma_1bit soma_1bit_5 (.A(S3_1), .B(and_5_out), .Ci(1'b0), .S(AC[4]), .Co(soma_1bit_5_co));
  soma_1bit soma_1bit_6 (.A(S4_1), .B(and_6_out), .Ci(1'b0), .S(AC[5]), .Co(soma_1bit_6_co));
  soma_1bit soma_1bit_7 (.A(S5_1), .B(and_7_out), .Ci(1'b0), .S(AC[6]), .Co(soma_1bit_7_co));
  soma_1bit soma_1bit_8 (.A(S6_1), .B(and_8_out), .Ci(1'b0), .S(AC[7]), .Co(soma_1bit_8_co));
  and and_9 (and_9_out, A[1], B[0]);
  and and_10 (and_10_out, A[1], B[1]);
  and and_11 (and_11_out, A[1], B[2]);
  and and_12 (and_12_out, A[1], B[3]);
  and and_13 (and_13_out, A[1], B[4]);
  and and_14 (and_14_out, A[1], B[5]);
  and and_15 (and_15_out, A[1], B[6]);
  and and_16 (and_16_out, A[1], B[7]);
  soma_1bit soma_1bit_9 (.A(1'b0), .B(and_9_out), .Ci(soma_1bit_1_co), .S(S0_1), .Co(soma_1bit_9_co));
  soma_1bit soma_1bit_10 (.A(S0_2), .B(and_10_out), .Ci(soma_1bit_2_co), .S(S1_1), .Co(soma_1bit_10_co));
  soma_1bit soma_1bit_11 (.A(S1_2), .B(and_11_out), .Ci(soma_1bit_3_co), .S(S2_1), .Co(soma_1bit_11_co));
  soma_1bit soma_1bit_12 (.A(S2_2), .B(and_12_out), .Ci(soma_1bit_4_co), .S(S3_1), .Co(soma_1bit_12_co));
  soma_1bit soma_1bit_13 (.A(S3_2), .B(and_13_out), .Ci(soma_1bit_5_co), .S(S4_1), .Co(soma_1bit_13_co));
  soma_1bit soma_1bit_14 (.A(S4_2), .B(and_14_out), .Ci(soma_1bit_6_co), .S(S5_1), .Co(soma_1bit_14_co));
  soma_1bit soma_1bit_15 (.A(S5_2), .B(and_15_out), .Ci(soma_1bit_7_co), .S(S6_1), .Co(soma_1bit_15_co));
  soma_1bit soma_1bit_16 (.A(S6_2), .B(and_16_out), .Ci(soma_1bit_8_co), .S(MQ[0]), .Co(soma_1bit_16_co));
  and and_17 (and_17_out, A[2], B[0]);
  and and_18 (and_18_out, A[2], B[1]);
  and and_19 (and_19_out, A[2], B[2]);
  and and_20 (and_20_out, A[2], B[3]);
  and and_21 (and_21_out, A[2], B[4]);
  and and_22 (and_22_out, A[2], B[5]);
  and and_23 (and_23_out, A[2], B[6]);
  and and_24 (and_24_out, A[2], B[7]);
  soma_1bit soma_1bit_17 (.A(1'b0), .B(and_17_out), .Ci(soma_1bit_9_co), .S(S0_2), .Co(soma_1bit_17_co));
  soma_1bit soma_1bit_18 (.A(S0_3), .B(and_18_out), .Ci(soma_1bit_10_co), .S(S1_2), .Co(soma_1bit_18_co));
  soma_1bit soma_1bit_19 (.A(S1_3), .B(and_19_out), .Ci(soma_1bit_11_co), .S(S2_2), .Co(soma_1bit_19_co));
  soma_1bit soma_1bit_20 (.A(S2_3), .B(and_20_out), .Ci(soma_1bit_12_co), .S(S3_2), .Co(soma_1bit_20_co));
  soma_1bit soma_1bit_21 (.A(S3_3), .B(and_21_out), .Ci(soma_1bit_13_co), .S(S4_2), .Co(soma_1bit_21_co));
  soma_1bit soma_1bit_22 (.A(S4_3), .B(and_22_out), .Ci(soma_1bit_14_co), .S(S5_2), .Co(soma_1bit_22_co));
  soma_1bit soma_1bit_23 (.A(S5_3), .B(and_23_out), .Ci(soma_1bit_15_co), .S(S6_2), .Co(soma_1bit_23_co));
  soma_1bit soma_1bit_24 (.A(S6_3), .B(and_24_out), .Ci(soma_1bit_16_co), .S(MQ[1]), .Co(soma_1bit_24_co));
  and and_25 (and_25_out, A[3], B[0]);
  and and_26 (and_26_out, A[3], B[1]);
  and and_27 (and_27_out, A[3], B[2]);
  and and_28 (and_28_out, A[3], B[3]);
  and and_29 (and_29_out, A[3], B[4]);
  and and_30 (and_30_out, A[3], B[5]);
  and and_31 (and_31_out, A[3], B[6]);
  and and_32 (and_32_out, A[3], B[7]);
  soma_1bit soma_1bit_25 (.A(1'b0), .B(and_25_out), .Ci(soma_1bit_17_co), .S(S0_3), .Co(soma_1bit_25_co));
  soma_1bit soma_1bit_26 (.A(S0_4), .B(and_26_out), .Ci(soma_1bit_18_co), .S(S1_3), .Co(soma_1bit_26_co));
  soma_1bit soma_1bit_27 (.A(S1_4), .B(and_27_out), .Ci(soma_1bit_19_co), .S(S2_3), .Co(soma_1bit_27_co));
  soma_1bit soma_1bit_28 (.A(S2_4), .B(and_28_out), .Ci(soma_1bit_20_co), .S(S3_3), .Co(soma_1bit_28_co));
  soma_1bit soma_1bit_29 (.A(S3_4), .B(and_29_out), .Ci(soma_1bit_21_co), .S(S4_3), .Co(soma_1bit_29_co));
  soma_1bit soma_1bit_30 (.A(S4_4), .B(and_30_out), .Ci(soma_1bit_22_co), .S(S5_3), .Co(soma_1bit_30_co));
  soma_1bit soma_1bit_31 (.A(S5_4), .B(and_31_out), .Ci(soma_1bit_23_co), .S(S6_3), .Co(soma_1bit_31_co));
  soma_1bit soma_1bit_32 (.A(S6_4), .B(and_32_out), .Ci(soma_1bit_24_co), .S(MQ[2]), .Co(soma_1bit_32_co));
  and and_33 (and_33_out, A[4], B[0]);
  and and_34 (and_34_out, A[4], B[1]);
  and and_35 (and_35_out, A[4], B[2]);
  and and_36 (and_36_out, A[4], B[3]);
  and and_37 (and_37_out, A[4], B[4]);
  and and_38 (and_38_out, A[4], B[5]);
  and and_39 (and_39_out, A[4], B[6]);
  and and_40 (and_40_out, A[4], B[7]);
  soma_1bit soma_1bit_33 (.A(1'b0), .B(and_33_out), .Ci(soma_1bit_25_co), .S(S0_4), .Co(soma_1bit_33_co));
  soma_1bit soma_1bit_34 (.A(S0_5), .B(and_34_out), .Ci(soma_1bit_26_co), .S(S1_4), .Co(soma_1bit_34_co));
  soma_1bit soma_1bit_35 (.A(S1_5), .B(and_35_out), .Ci(soma_1bit_27_co), .S(S2_4), .Co(soma_1bit_35_co));
  soma_1bit soma_1bit_36 (.A(S2_5), .B(and_36_out), .Ci(soma_1bit_28_co), .S(S3_4), .Co(soma_1bit_36_co));
  soma_1bit soma_1bit_37 (.A(S3_5), .B(and_37_out), .Ci(soma_1bit_29_co), .S(S4_4), .Co(soma_1bit_37_co));
  soma_1bit soma_1bit_38 (.A(S4_5), .B(and_38_out), .Ci(soma_1bit_30_co), .S(S5_4), .Co(soma_1bit_38_co));
  soma_1bit soma_1bit_39 (.A(S5_5), .B(and_39_out), .Ci(soma_1bit_31_co), .S(S6_4), .Co(soma_1bit_39_co));
  soma_1bit soma_1bit_40 (.A(S6_5), .B(and_40_out), .Ci(soma_1bit_32_co), .S(MQ[3]), .Co(soma_1bit_40_co));
  and and_41 (and_41_out, A[5], B[0]);
  and and_42 (and_42_out, A[5], B[1]);
  and and_43 (and_43_out, A[5], B[2]);
  and and_44 (and_44_out, A[5], B[3]);
  and and_45 (and_45_out, A[5], B[4]);
  and and_46 (and_46_out, A[5], B[5]);
  and and_47 (and_47_out, A[5], B[6]);
  and and_48 (and_48_out, A[5], B[7]);
  soma_1bit soma_1bit_41 (.A(1'b0), .B(and_41_out), .Ci(soma_1bit_33_co), .S(S0_5), .Co(soma_1bit_41_co));
  soma_1bit soma_1bit_42 (.A(S0_6), .B(and_42_out), .Ci(soma_1bit_34_co), .S(S1_5), .Co(soma_1bit_42_co));
  soma_1bit soma_1bit_43 (.A(S3_6), .B(and_43_out), .Ci(soma_1bit_35_co), .S(S2_5), .Co(soma_1bit_43_co));
  soma_1bit soma_1bit_44 (.A(S2_6), .B(and_44_out), .Ci(soma_1bit_36_co), .S(S3_5), .Co(soma_1bit_44_co));
  soma_1bit soma_1bit_45 (.A(S3_6), .B(and_45_out), .Ci(soma_1bit_37_co), .S(S4_5), .Co(soma_1bit_45_co));
  soma_1bit soma_1bit_46 (.A(S4_6), .B(and_46_out), .Ci(soma_1bit_38_co), .S(S5_5), .Co(soma_1bit_46_co));
  soma_1bit soma_1bit_47 (.A(S5_6), .B(and_47_out), .Ci(soma_1bit_39_co), .S(S6_5), .Co(soma_1bit_47_co));
  soma_1bit soma_1bit_48 (.A(S6_6), .B(and_48_out), .Ci(soma_1bit_40_co), .S(MQ[4]), .Co(soma_1bit_48_co));
  and and_49 (and_49_out, A[6], B[0]);
  and and_50 (and_50_out, A[6], B[1]);
  and and_51 (and_51_out, A[6], B[2]);
  and and_52 (and_52_out, A[6], B[3]);
  and and_53 (and_53_out, A[6], B[4]);
  and and_54 (and_54_out, A[6], B[5]);
  and and_55 (and_55_out, A[6], B[6]);
  and and_56 (and_56_out, A[6], B[7]);
  soma_1bit soma_1bit_49 (.A(1'b0), .B(and_49_out), .Ci(soma_1bit_41_co), .S(S0_6), .Co(soma_1bit_49_co));
  soma_1bit soma_1bit_50 (.A(S0_7), .B(and_50_out), .Ci(soma_1bit_42_co), .S(S1_6), .Co(soma_1bit_50_co));
  soma_1bit soma_1bit_51 (.A(S1_7), .B(and_51_out), .Ci(soma_1bit_43_co), .S(S2_6), .Co(soma_1bit_51_co));
  soma_1bit soma_1bit_52 (.A(S2_7), .B(and_52_out), .Ci(soma_1bit_44_co), .S(S3_6), .Co(soma_1bit_52_co));
  soma_1bit soma_1bit_53 (.A(S3_7), .B(and_53_out), .Ci(soma_1bit_45_co), .S(S4_6), .Co(soma_1bit_53_co));
  soma_1bit soma_1bit_54 (.A(S4_7), .B(and_54_out), .Ci(soma_1bit_46_co), .S(S5_6), .Co(soma_1bit_54_co));
  soma_1bit soma_1bit_55 (.A(S5_7), .B(and_55_out), .Ci(soma_1bit_47_co), .S(S6_6), .Co(soma_1bit_55_co));
  soma_1bit soma_1bit_56 (.A(S6_7), .B(and_56_out), .Ci(soma_1bit_48_co), .S(MQ[5]), .Co(soma_1bit_56_co));
  and and_57 (and_57_out, A[7], B[0]);
  and and_58 (and_58_out, A[7], B[1]);
  and and_59 (and_59_out, A[7], B[2]);
  and and_60 (and_60_out, A[7], B[3]);
  and and_61 (and_61_out, A[7], B[4]);
  and and_62 (and_62_out, A[7], B[5]);
  and and_63 (and_63_out, A[7], B[6]);
  and and_64 (and_64_out, A[7], B[7]);
  soma_1bit soma_1bit_57 (.A(1'b0), .B(and_57_out), .Ci(soma_1bit_49_co), .S(S0_7), .Co(Co_0));
  soma_1bit soma_1bit_58 (.A(Co_0), .B(and_58_out), .Ci(soma_1bit_50_co), .S(S1_7), .Co(Co_1));
  soma_1bit soma_1bit_59 (.A(Co_1), .B(and_59_out), .Ci(soma_1bit_51_co), .S(S2_7), .Co(Co_2));
  soma_1bit soma_1bit_60 (.A(Co_2), .B(and_60_out), .Ci(soma_1bit_52_co), .S(S3_7), .Co(Co_3));
  soma_1bit soma_1bit_61 (.A(Co_3), .B(and_61_out), .Ci(soma_1bit_53_co), .S(S4_7), .Co(Co_4));
  soma_1bit soma_1bit_62 (.A(Co_4), .B(and_62_out), .Ci(soma_1bit_54_co), .S(S5_7), .Co(Co_5));
  soma_1bit soma_1bit_63 (.A(Co_5), .B(and_63_out), .Ci(soma_1bit_55_co), .S(S6_7), .Co(Co_6));
  soma_1bit soma_1bit_64 (.A(Co_6), .B(and_64_out), .Ci(soma_1bit_56_co), .S(MQ[6]), .Co(MQ[7]));

  // Other names for the same wires on the sheet: Co_7 = MQ[7]; S0_0 = AC[0]; S1_0 = AC[1]; S2_0 = AC[2]; S3_0 = AC[3];
  //   S4_0 = AC[4]; S5_0 = AC[5]; S6_0 = AC[6]; S7_0 = AC[7]; S7_1 = MQ[0]; S7_2 = MQ[1]; S7_3 = MQ[2]; S7_4 = MQ[3];
  //   S7_5 = MQ[4]; S7_6 = MQ[5]; S7_7 = MQ[6]
endmodule
