// Digital circuit shift.dig as structural Verilog
module shift (
  input  [7:0] A,
  input  Dir,
  output [7:0] out_3
);

  Multiplexer #(.Bits(8)) multiplexer_1 (.sel(Dir), .in_0({A[6:0], 1'b0}), .in_1({1'b0, A[7:1]}), .out(out_3));
endmodule
