// Digital circuit soma_AC.dig as structural Verilog
module soma_AC (
  input  [7:0] B,
  output [3:0] S1,
  output [3:0] S2
);

  wire button_1_out, soma_1bit_1_co, soma_1bit_1_s, soma_1bit_2_co, soma_1bit_2_s, soma_1bit_3_co,
       soma_1bit_3_s, soma_1bit_4_co, soma_1bit_4_s, soma_1bit_5_co, soma_1bit_5_s, soma_1bit_6_co,
       soma_1bit_6_s, soma_1bit_7_co, soma_1bit_7_s, soma_1bit_8_co, soma_1bit_8_s;

  soma_1bit soma_1bit_1 (.A(S1[0]), .B(B[0]), .Ci(1'b0), .S(soma_1bit_1_s), .Co(soma_1bit_1_co));
  soma_1bit soma_1bit_2 (.A(S1[1]), .B(B[1]), .Ci(soma_1bit_1_co), .S(soma_1bit_2_s), .Co(soma_1bit_2_co));
  soma_1bit soma_1bit_3 (.A(S1[2]), .B(B[2]), .Ci(soma_1bit_2_co), .S(soma_1bit_3_s), .Co(soma_1bit_3_co));
  soma_1bit soma_1bit_4 (.A(S1[3]), .B(B[3]), .Ci(soma_1bit_3_co), .S(soma_1bit_4_s), .Co(soma_1bit_4_co));
  soma_1bit soma_1bit_5 (.A(S2[0]), .B(B[4]), .Ci(soma_1bit_4_co), .S(soma_1bit_5_s), .Co(soma_1bit_5_co));
  soma_1bit soma_1bit_6 (.A(S2[1]), .B(B[5]), .Ci(soma_1bit_5_co), .S(soma_1bit_6_s), .Co(soma_1bit_6_co));
  soma_1bit soma_1bit_7 (.A(S2[2]), .B(B[6]), .Ci(soma_1bit_6_co), .S(soma_1bit_7_s), .Co(soma_1bit_7_co));
  soma_1bit soma_1bit_8 (.A(S2[3]), .B(B[7]), .Ci(soma_1bit_7_co), .S(soma_1bit_8_s), .Co(soma_1bit_8_co));
  Button button_1 (.out(button_1_out));
  D_FF d_ff_1 (.D(soma_1bit_1_s), .C(button_1_out), .Q(S1[0]));  // open: nQ
  D_FF d_ff_2 (.D(soma_1bit_2_s), .C(button_1_out), .Q(S1[1]));  // open: nQ
  D_FF d_ff_3 (.D(soma_1bit_3_s), .C(button_1_out), .Q(S1[2]));  // open: nQ
  D_FF d_ff_4 (.D(soma_1bit_4_s), .C(button_1_out), .Q(S1[3]));  // open: nQ
  D_FF d_ff_5 (.D(soma_1bit_5_s), .C(button_1_out), .Q(S2[0]));  // open: nQ
  D_FF d_ff_6 (.D(soma_1bit_6_s), .C(button_1_out), .Q(S2[1]));  // open: nQ
  D_FF d_ff_7 (.D(soma_1bit_7_s), .C(button_1_out), .Q(S2[2]));  // open: nQ
  D_FF d_ff_8 (.D(soma_1bit_8_s), .C(button_1_out), .Q(S2[3]));  // open: nQ
  // also tied to GND on the sheet: soma_1bit_8_co

  // Other names for the same wires on the sheet: Q0 = S1[0]; Q1 = S1[1]; Q2 = S1[2]; Q3 = S1[3]; Q4 = S2[0];
  //   Q5 = S2[1]; Q6 = S2[2]; Q7 = S2[3]
endmodule
