// Digital circuit subtracao_8bit.dig as structural Verilog
module subtracao_8bit (
  input  [7:0] A,
  input  [7:0] B,
  input  Sel,
  output [3:0] S1,
  output Co,
  output [3:0] S2
);

  wire soma_1bit_1_co, soma_1bit_2_co, soma_1bit_3_co, soma_1bit_4_co, soma_1bit_5_co, soma_1bit_6_co,
       soma_1bit_7_co, xor_1_out, xor_2_out, xor_3_out, xor_4_out, xor_5_out, xor_6_out, xor_7_out, xor_8_out;

  xor xor_1 (xor_1_out, B[0], Sel);
  xor xor_2 (xor_2_out, B[1], Sel);
  xor xor_3 (xor_3_out, B[2], Sel);
  xor xor_4 (xor_4_out, B[3], Sel);
  xor xor_5 (xor_5_out, B[4], Sel);
  xor xor_6 (xor_6_out, B[5], Sel);
  xor xor_7 (xor_7_out, B[6], Sel);
  xor xor_8 (xor_8_out, B[7], Sel);
  soma_1bit soma_1bit_1 (.A(A[0]), .B(xor_1_out), .Ci(Sel), .S(S1[0]), .Co(soma_1bit_1_co));
  soma_1bit soma_1bit_2 (.A(A[1]), .B(xor_2_out), .Ci(soma_1bit_1_co), .S(S1[1]), .Co(soma_1bit_2_co));
  soma_1bit soma_1bit_3 (.A(A[2]), .B(xor_3_out), .Ci(soma_1bit_2_co), .S(S1[2]), .Co(soma_1bit_3_co));
  soma_1bit soma_1bit_4 (.A(A[3]), .B(xor_4_out), .Ci(soma_1bit_3_co), .S(S1[3]), .Co(soma_1bit_4_co));
  soma_1bit soma_1bit_5 (.A(A[4]), .B(xor_5_out), .Ci(soma_1bit_4_co), .S(S2[0]), .Co(soma_1bit_5_co));
  soma_1bit soma_1bit_6 (.A(A[5]), .B(xor_6_out), .Ci(soma_1bit_5_co), .S(S2[1]), .Co(soma_1bit_6_co));
  soma_1bit soma_1bit_7 (.A(A[6]), .B(xor_7_out), .Ci(soma_1bit_6_co), .S(S2[2]), .Co(soma_1bit_7_co));
  soma_1bit soma_1bit_8 (.A(A[7]), .B(xor_8_out), .Ci(soma_1bit_7_co), .S(S2[3]), .Co(Co));
endmodule
