// Digital circuit subtracao_restauracao.dig as structural Verilog
module subtracao_restauracao (
  input  A,
  input  B,
  input  Ci,
  input  Sel,
  output Co,
  output R
);

  wire B_t, soma_1bit_1_s;

  not not_1 (B_t, B);
  soma_1bit soma_1bit_1 (.A(A), .B(B_t), .Ci(Ci), .S(soma_1bit_1_s), .Co(Co));
  Multiplexer multiplexer_1 (.sel(Sel), .in_0(A), .in_1(soma_1bit_1_s), .out(R));
endmodule
